# Fritzing sketch mac_clock_schematic (saved by Fritzing 1.0.5)

parts:
  WeMos_D1_Mini1 = WeMos D1 Mini
  OLED_I2C1 = OLED 128x64 I2C Monochrome Display
  S1 = Pushbutton [package=THT]

nets:
  3V3: WeMos_D1_Mini1.3V3, OLED_I2C1.VDD
  N1: WeMos_D1_Mini1.D1, OLED_I2C1.SCK
  N2: WeMos_D1_Mini1.D2, OLED_I2C1.SDA
  N3: WeMos_D1_Mini1.D5, S1.leg1
  N4: WeMos_D1_Mini1.G, OLED_I2C1.GND, S1.leg0
